// Logisim project stack_logical_normal.circ as structural Verilog: 15 circuits, main circuit main
module main (
  input  CLK,
  input  RESET,
  input  [1:0] COMMAND,
  input  [2:0] INDEX,
  input  [3:0] IO_DATA_in,
  output [3:0] IO_DATA_out
);

  wire [3:0] stack_1_d0, stack_1_d1, stack_1_d2, stack_1_d3, stack_1_d4;

  // Probe on stack_1_d0
  stack stack_1 (
    .CLK(CLK), .RESET(RESET), .COMMAND(COMMAND), .INDEX(INDEX), .IO_DATA_in(IO_DATA_in), .d0(stack_1_d0),
    .d1(stack_1_d1), .d2(stack_1_d2), .d3(stack_1_d3), .d4(stack_1_d4), .IO_DATA_out(IO_DATA_out));
  // Probe on stack_1_d1
  // Probe on stack_1_d2
  // Probe on stack_1_d3
  // Probe on stack_1_d4
endmodule

module stack (
  input  CLK,
  input  RESET,
  input  [1:0] COMMAND,
  input  [2:0] INDEX,
  input  [3:0] IO_DATA_in,
  output [3:0] d0,
  output [3:0] d1,
  output [3:0] d2,
  output [3:0] d3,
  output [3:0] d4,
  output [3:0] IO_DATA_out
);

  wire and_1_out, and_2_out, and_3_out, and_4_out, and_5_out, and_6_out, and_10_out, and_11_out, and_12_out,
       and_13_out, and_14_out, decode_3_bits_to_mod_5_1_q0, decode_3_bits_to_mod_5_1_q1,
       decode_3_bits_to_mod_5_1_q2, decode_3_bits_to_mod_5_1_q3, decode_3_bits_to_mod_5_1_q4, not_1_out,
       or_1_out;
  wire [0:0] or_2_out;
  wire [2:0] and_7_out, head_1_q, sub_1_q, sub_2_q;
  wire [3:0] mem_6_res, mux_get_mem_1_q;

  and and_1 (and_1_out, COMMAND[0], COMMAND[1]);
  and and_2 (and_2_out, ~COMMAND[0], COMMAND[1]);  // AND_Gate
  and and_3 (and_3_out, COMMAND[0], COMMAND[1]);
  and and_4 (and_4_out, ~COMMAND[0], COMMAND[1]);  // AND_Gate
  or or_1 (or_1_out, and_1_out, and_2_out);
  or or_2 (or_2_out[0], and_3_out, and_4_out);
  and and_5 (and_5_out, COMMAND[0], COMMAND[1]);
  not not_1 (not_1_out, and_6_out);
  and and_6 (and_6_out, CLK, or_1_out);
  head head_1 (.CMD(COMMAND), .CLK(CLK), .RESET(RESET), .Q(head_1_q));
  and and_7 (and_7_out[0], and_5_out, INDEX[0]);
  and and_8 (and_7_out[1], and_5_out, INDEX[1]);
  and and_9 (and_7_out[2], and_5_out, INDEX[2]);
  Transistor #(.width(4)) transistor_1 (.in(mem_6_res), .out(IO_DATA_in), .gate(not_1_out));
  Transistor #(.\type ("n"), .width(4)) transistor_2 (.in(mem_6_res), .out(IO_DATA_in), .gate(and_6_out));
  SUB sub_1 (.A(head_1_q), .B(and_7_out), .Q(sub_1_q));
  SUB sub_2 (.A(sub_1_q), .B({2'b00, or_2_out[0]}), .Q(sub_2_q));
  decode_3_bits_to_mod_5 decode_3_bits_to_mod_5_1 (
    .A0(head_1_q[0]), .A1(head_1_q[1]), .A2(head_1_q[2]), .Q0(decode_3_bits_to_mod_5_1_q0),
    .Q1(decode_3_bits_to_mod_5_1_q1), .Q2(decode_3_bits_to_mod_5_1_q2), .Q3(decode_3_bits_to_mod_5_1_q3),
    .Q4(decode_3_bits_to_mod_5_1_q4));
  and and_10 (and_10_out, CLK, decode_3_bits_to_mod_5_1_q0);
  and and_11 (and_11_out, CLK, decode_3_bits_to_mod_5_1_q1);
  and and_12 (and_12_out, CLK, decode_3_bits_to_mod_5_1_q2);
  and and_13 (and_13_out, CLK, decode_3_bits_to_mod_5_1_q3);
  and and_14 (and_14_out, CLK, decode_3_bits_to_mod_5_1_q4);
  MEM mem_1 (.Cmd(COMMAND), .C(and_10_out), .D(IO_DATA_in), .RESET(RESET), .res(d0));
  MEM mem_2 (.Cmd(COMMAND), .C(and_11_out), .D(IO_DATA_in), .RESET(RESET), .res(d1));
  MEM mem_3 (.Cmd(COMMAND), .C(and_12_out), .D(IO_DATA_in), .RESET(RESET), .res(d2));
  MEM mem_4 (.Cmd(COMMAND), .C(and_13_out), .D(IO_DATA_in), .RESET(RESET), .res(d3));
  MEM mem_5 (.Cmd(COMMAND), .C(and_14_out), .D(IO_DATA_in), .RESET(RESET), .res(d4));
  mux_get_MEM mux_get_mem_1 (
    .A0(sub_2_q[0]), .A1(sub_2_q[1]), .A2(sub_2_q[2]), .D0(d0), .D1(d1), .D2(d2), .D3(d3), .D4(d4),
    .Q(mux_get_mem_1_q));
  MEM mem_6 (.Cmd(2'b01), .C(CLK), .D(mux_get_mem_1_q), .RESET(RESET), .res(mem_6_res));

  assign IO_DATA_out = IO_DATA_in;

  // Notes on the sheet:
  //   your circuit must be here
endmodule

module MEM (
  input  [1:0] Cmd,
  input  C,
  input  [3:0] D,
  input  RESET,
  output [3:0] res
);

  wire and_1_out, and_2_out;

  and and_1 (and_1_out, ~Cmd[1], Cmd[0]);  // AND_Gate
  and and_2 (and_2_out, and_1_out, C);
  D_Trigger d_trigger_1 (.C(and_2_out), .D(D[0]), .RESET(RESET), .Q(res[0]));  // open: NQ
  D_Trigger d_trigger_2 (.C(and_2_out), .D(D[1]), .RESET(RESET), .Q(res[1]));  // open: NQ
  D_Trigger d_trigger_3 (.C(and_2_out), .D(D[2]), .RESET(RESET), .Q(res[2]));  // open: NQ
  D_Trigger d_trigger_4 (.C(and_2_out), .D(D[3]), .RESET(RESET), .Q(res[3]));  // open: NQ
endmodule

module D_Trigger (
  input  C,
  input  D,
  input  RESET,
  output Q,
  output NQ
);

  wire and_1_out, not_1_out, or_1_out;

  and and_1 (and_1_out, D, ~RESET);  // AND_Gate
  or or_1 (or_1_out, C, RESET);
  not not_1 (not_1_out, and_1_out);
  RS_Trigger_Sync rs_trigger_sync_1 (.R(not_1_out), .C(or_1_out), .S(and_1_out), .Q(Q), .NQ(NQ));
endmodule

module RS_Trigger_Sync (
  input  R,
  input  C,
  input  S,
  output Q,
  output NQ
);

  wire and_1_out, and_2_out, nor_2_out, por_1_out;

  and and_1 (and_1_out, R, C);
  and and_2 (and_2_out, C, S);
  nor nor_1 (Q, and_1_out, NQ);
  nor nor_2 (nor_2_out, Q, and_2_out);
  POR por_1 (.out(por_1_out));
  xor xor_1 (NQ, nor_2_out, por_1_out);
endmodule

module SUM (
  input  [2:0] A,
  input  [2:0] B,
  output [2:0] Q
);

  wire and_1_out, and_2_out, and_3_out, and_4_out, and_5_out, and_6_out, and_7_out, and_8_out, and_9_out,
       and_10_out, and_11_out, and_12_out, and_13_out, and_14_out, and_15_out, and_16_out, and_17_out,
       and_18_out, and_19_out, and_20_out, and_21_out, and_22_out, and_23_out, and_24_out, and_25_out,
       decode_3_bits_to_mod_5_1_q0, decode_3_bits_to_mod_5_1_q1, decode_3_bits_to_mod_5_1_q2,
       decode_3_bits_to_mod_5_1_q3, decode_3_bits_to_mod_5_1_q4, decode_3_bits_to_mod_5_2_q0,
       decode_3_bits_to_mod_5_2_q1, decode_3_bits_to_mod_5_2_q2, decode_3_bits_to_mod_5_2_q3,
       decode_3_bits_to_mod_5_2_q4, or_1_out, or_2_out, or_3_out, or_4_out, or_5_out;

  decode_3_bits_to_mod_5 decode_3_bits_to_mod_5_1 (
    .A0(A[0]), .A1(A[1]), .A2(A[2]), .Q0(decode_3_bits_to_mod_5_1_q0), .Q1(decode_3_bits_to_mod_5_1_q1),
    .Q2(decode_3_bits_to_mod_5_1_q2), .Q3(decode_3_bits_to_mod_5_1_q3), .Q4(decode_3_bits_to_mod_5_1_q4));
  decode_3_bits_to_mod_5 decode_3_bits_to_mod_5_2 (
    .A0(B[0]), .A1(B[1]), .A2(B[2]), .Q0(decode_3_bits_to_mod_5_2_q0), .Q1(decode_3_bits_to_mod_5_2_q1),
    .Q2(decode_3_bits_to_mod_5_2_q2), .Q3(decode_3_bits_to_mod_5_2_q3), .Q4(decode_3_bits_to_mod_5_2_q4));
  and and_1 (and_1_out, decode_3_bits_to_mod_5_1_q0, decode_3_bits_to_mod_5_2_q4);
  and and_2 (and_2_out, decode_3_bits_to_mod_5_1_q1, decode_3_bits_to_mod_5_2_q3);
  and and_3 (and_3_out, decode_3_bits_to_mod_5_1_q2, decode_3_bits_to_mod_5_2_q2);
  and and_4 (and_4_out, decode_3_bits_to_mod_5_1_q3, decode_3_bits_to_mod_5_2_q1);
  and and_5 (and_5_out, decode_3_bits_to_mod_5_1_q4, decode_3_bits_to_mod_5_2_q0);
  or or_1 (or_1_out, and_1_out, and_2_out, and_3_out, and_4_out, and_5_out);
  and and_6 (and_6_out, decode_3_bits_to_mod_5_1_q0, decode_3_bits_to_mod_5_2_q3);
  and and_7 (and_7_out, decode_3_bits_to_mod_5_1_q1, decode_3_bits_to_mod_5_2_q2);
  and and_8 (and_8_out, decode_3_bits_to_mod_5_1_q2, decode_3_bits_to_mod_5_2_q1);
  and and_9 (and_9_out, decode_3_bits_to_mod_5_1_q3, decode_3_bits_to_mod_5_2_q0);
  and and_10 (and_10_out, decode_3_bits_to_mod_5_1_q4, decode_3_bits_to_mod_5_2_q4);
  or or_2 (or_2_out, and_6_out, and_7_out, and_8_out, and_9_out, and_10_out);
  and and_11 (and_11_out, decode_3_bits_to_mod_5_1_q0, decode_3_bits_to_mod_5_2_q2);
  and and_12 (and_12_out, decode_3_bits_to_mod_5_1_q1, decode_3_bits_to_mod_5_2_q1);
  and and_13 (and_13_out, decode_3_bits_to_mod_5_1_q2, decode_3_bits_to_mod_5_2_q0);
  and and_14 (and_14_out, decode_3_bits_to_mod_5_1_q3, decode_3_bits_to_mod_5_2_q4);
  and and_15 (and_15_out, decode_3_bits_to_mod_5_1_q4, decode_3_bits_to_mod_5_2_q3);
  and and_16 (and_16_out, decode_3_bits_to_mod_5_1_q0, decode_3_bits_to_mod_5_2_q0);
  and and_17 (and_17_out, decode_3_bits_to_mod_5_1_q1, decode_3_bits_to_mod_5_2_q4);
  and and_18 (and_18_out, decode_3_bits_to_mod_5_1_q2, decode_3_bits_to_mod_5_2_q3);
  and and_19 (and_19_out, decode_3_bits_to_mod_5_1_q3, decode_3_bits_to_mod_5_2_q2);
  and and_20 (and_20_out, decode_3_bits_to_mod_5_1_q4, decode_3_bits_to_mod_5_2_q1);
  or or_3 (or_3_out, and_11_out, and_12_out, and_13_out, and_14_out, and_15_out);
  or or_4 (or_4_out, and_16_out, and_17_out, and_18_out, and_19_out, and_20_out);
  and and_21 (and_21_out, decode_3_bits_to_mod_5_1_q0, decode_3_bits_to_mod_5_2_q1);
  and and_22 (and_22_out, decode_3_bits_to_mod_5_1_q4, decode_3_bits_to_mod_5_2_q2);
  and and_23 (and_23_out, decode_3_bits_to_mod_5_1_q3, decode_3_bits_to_mod_5_2_q3);
  and and_24 (and_24_out, decode_3_bits_to_mod_5_1_q2, decode_3_bits_to_mod_5_2_q4);
  and and_25 (and_25_out, decode_3_bits_to_mod_5_1_q1, decode_3_bits_to_mod_5_2_q0);
  or or_5 (or_5_out, and_21_out, and_22_out, and_23_out, and_24_out, and_25_out);
  encode_mod_5_to_3_bits encode_mod_5_to_3_bits_1 (
    .Q0(or_4_out), .Q1(or_5_out), .Q2(or_3_out), .Q3(or_2_out), .Q4(or_1_out), .A0(Q[0]), .A1(Q[1]), .A2(Q[2]));
endmodule

module decode_3_bits_to_mod_5 (
  input  A0,
  input  A1,
  input  A2,
  output Q0,
  output Q1,
  output Q2,
  output Q3,
  output Q4
);

  wire and_1_out, and_2_out, and_3_out, and_6_out, and_7_out, and_8_out;

  and and_1 (and_1_out, ~A0, ~A1, ~A2);  // AND_Gate
  and and_2 (and_2_out, A0, ~A1, ~A2);  // AND_Gate
  and and_3 (and_3_out, ~A0, A1, ~A2);  // AND_Gate
  and and_4 (Q3, A0, A1, ~A2);  // AND_Gate
  and and_5 (Q4, ~A0, ~A1, A2);  // AND_Gate
  and and_6 (and_6_out, A0, ~A1, A2);  // AND_Gate
  and and_7 (and_7_out, ~A0, A1, A2);  // AND_Gate
  and and_8 (and_8_out, A0, A1, A2);
  or or_1 (Q0, and_1_out, and_6_out);
  or or_2 (Q1, and_2_out, and_7_out);
  or or_3 (Q2, and_3_out, and_8_out);
endmodule

module encode_mod_5_to_3_bits (
  input  Q0,
  input  Q1,
  input  Q2,
  input  Q3,
  input  Q4,
  output A0,
  output A1,
  output A2
);

  or or_1 (A0, Q3, Q1);
  or or_2 (A1, Q2, Q3);

  assign A2 = Q4;
endmodule

module head (
  input  [1:0] CMD,
  input  CLK,
  input  RESET,
  output [2:0] Q
);

  wire [2:0] and_1_out, sum_1_q;

  and and_1 (and_1_out[0], CMD[0], ~CMD[1]);  // AND_Gate
  and and_2 (and_1_out[2], ~CMD[0], CMD[1]);  // AND_Gate
  counter counter_1 (.Cmd(2'b01), .C(CLK), .D(sum_1_q), .RESET(RESET), .res(Q));
  SUM sum_1 (.A({and_1_out[2], 1'b0, and_1_out[0]}), .B(Q), .Q(sum_1_q));
endmodule

module counter (
  input  [1:0] Cmd,
  input  C,
  input  [2:0] D,
  input  RESET,
  output [2:0] res
);

  wire and_1_out, and_2_out;

  and and_1 (and_1_out, ~Cmd[1], Cmd[0]);  // AND_Gate
  and and_2 (and_2_out, and_1_out, C);
  D_Trigger_Front_Sync d_trigger_front_sync_1 (.D(D[0]), .C(and_2_out), .RESET(RESET), .Q(res[0]));  // open: NQ
  D_Trigger_Front_Sync d_trigger_front_sync_2 (.D(D[1]), .C(and_2_out), .RESET(RESET), .Q(res[1]));  // open: NQ
  D_Trigger_Front_Sync d_trigger_front_sync_3 (.D(D[2]), .C(and_2_out), .RESET(RESET), .Q(res[2]));  // open: NQ
endmodule

module D_Trigger_Front_Sync (
  input  D,
  input  C,
  input  RESET,
  output Q,
  output NQ
);

  wire d_trigger_1_q, not_1_out;

  not not_1 (not_1_out, C);
  D_Trigger d_trigger_1 (.C(C), .D(D), .RESET(RESET), .Q(d_trigger_1_q));  // open: NQ
  D_Trigger d_trigger_2 (.C(not_1_out), .D(d_trigger_1_q), .RESET(RESET), .Q(Q), .NQ(NQ));
endmodule

module and_1_4_bits (
  input  A,
  input  [3:0] D,
  output [3:0] Q
);

  and and_1 (Q[0], A, D[0]);
  and and_2 (Q[1], A, D[1]);
  and and_3 (Q[2], A, D[2]);
  and and_4 (Q[3], A, D[3]);
endmodule

module mux_get_MEM (
  input  A0,
  input  A1,
  input  A2,
  input  [3:0] D0,
  input  [3:0] D1,
  input  [3:0] D2,
  input  [3:0] D3,
  input  [3:0] D4,
  output [3:0] Q
);

  wire decode_3_bits_to_mod_5_1_q0, decode_3_bits_to_mod_5_1_q1, decode_3_bits_to_mod_5_1_q2,
       decode_3_bits_to_mod_5_1_q3, decode_3_bits_to_mod_5_1_q4;
  wire [3:0] and_1_4_bits_1_q, and_1_4_bits_2_q, and_1_4_bits_3_q, and_1_4_bits_4_q, and_1_4_bits_5_q;

  decode_3_bits_to_mod_5 decode_3_bits_to_mod_5_1 (
    .A0(A0), .A1(A1), .A2(A2), .Q0(decode_3_bits_to_mod_5_1_q0), .Q1(decode_3_bits_to_mod_5_1_q1),
    .Q2(decode_3_bits_to_mod_5_1_q2), .Q3(decode_3_bits_to_mod_5_1_q3), .Q4(decode_3_bits_to_mod_5_1_q4));
  and_1_4_bits and_1_4_bits_1 (.A(decode_3_bits_to_mod_5_1_q0), .D(D0), .Q(and_1_4_bits_1_q));
  and_1_4_bits and_1_4_bits_2 (.A(decode_3_bits_to_mod_5_1_q1), .D(D1), .Q(and_1_4_bits_2_q));
  and_1_4_bits and_1_4_bits_3 (.A(decode_3_bits_to_mod_5_1_q2), .D(D2), .Q(and_1_4_bits_3_q));
  and_1_4_bits and_1_4_bits_4 (.A(decode_3_bits_to_mod_5_1_q3), .D(D3), .Q(and_1_4_bits_4_q));
  and_1_4_bits and_1_4_bits_5 (.A(decode_3_bits_to_mod_5_1_q4), .D(D4), .Q(and_1_4_bits_5_q));
  or_five_4bits or_five_4bits_1 (
    .D0(and_1_4_bits_1_q), .D1(and_1_4_bits_2_q), .D2(and_1_4_bits_3_q), .D3(and_1_4_bits_4_q),
    .D4(and_1_4_bits_5_q), .Q(Q));
endmodule

module or_five_4bits (
  input  [3:0] D0,
  input  [3:0] D1,
  input  [3:0] D2,
  input  [3:0] D3,
  input  [3:0] D4,
  output [3:0] Q
);

  or or_1 (Q[0], D0[0], D1[0], D2[0], D3[0], D4[0]);
  or or_2 (Q[1], D0[1], D1[1], D2[1], D3[1], D4[1]);
  or or_3 (Q[2], D0[2], D1[2], D2[2], D3[2], D4[2]);
  or or_4 (Q[3], D0[3], D1[3], D2[3], D3[3], D4[3]);
endmodule

module SUB (
  input  [2:0] A,
  input  [2:0] B,
  output [2:0] Q
);

  wire [2:0] sum_1_q, sum_2_q;

  SUM sum_1 (.A(A), .B({B[0], 2'b00}), .Q(sum_1_q));
  SUM sum_2 (.A(sum_1_q), .B({1'b0, {2{B[1]}}}), .Q(sum_2_q));
  SUM sum_3 (.A(sum_2_q), .B({2'b00, B[2]}), .Q(Q));
endmodule
